# Fritzing sketch climatemood wiring (saved by Fritzing 0.9.10b)
circuit board: 8.46667cm x 5.64444cm
breadboards: 1

parts:
  Grove1 = Grove OLED 128x96
  RHT1 = Humidity and Temperature Sensor RHT03
  元件2 = Adafruit HUZZAH32 ESP32 Feather [part_number="Adafruit #3405"]
  J2 = Basic Servo

nets:
  GND: Grove1.GND, RHT1.GND_2, 元件2.GND, 元件2.N/C, J2.gnd
  VCC: Grove1.VCC, RHT1.Vcc, 元件2.3.3V, 元件2.RESET, J2.vcc
  N1: Grove1.SDA, 元件2.SDA
  N2: Grove1.SCL, 元件2.SCL
  N3: RHT1.Data-signal, 元件2.IO14_A6
